// Logisim project log.circ as structural Verilog
module main (
  input  in_1,
  input  in_2,
  input  in_3,
  input  in_4,
  input  in_5,
  input  in_6,
  input  in_7,
  input  in_8,
  input  in_9,
  input  in_10,
  input  [2:0] in_11,
  input  [2:0] in_12,
  input  [1:0] GT__EQ
);

  wire clock_1_out, decoder_1_out0, decoder_1_out1, decoder_1_out2, decoder_1_out3, not_1_out, or_1_out;
  wire [1:0] t_ff_1_q;
  wire [3:0] counter_1_q;
  wire [7:0] controlled_buffer_1_out, regdec_1_out_5, regdec_1_out_5_2, register_1_q, register_2_q,
       register_3_q, register_4_q, register_5_q, register_6_q, register_8_q, register_9_q, register_11_q;
  wire [15:0] controlled_buffer_9_out, counter_2_q, register_7_q, register_10_q, shreg_1_out_3;

  assign controlled_buffer_1_out = regdec_1_out_5_2[6] ? register_1_q : 8'bz;  // Controlled_Buffer controlled_buffer_1
  Register register_1 (.Q(register_1_q), .clk(regdec_1_out_5_2[7]));  // open: D, en, clr
  Register register_2 (.D(controlled_buffer_1_out), .Q(register_2_q), .clk(regdec_1_out_5_2[5]));  // open: en, clr
  assign controlled_buffer_1_out = regdec_1_out_5_2[4] ? register_2_q : 8'bz;  // Controlled_Buffer controlled_buffer_2
  Register register_3 (.D(controlled_buffer_1_out), .Q(register_3_q), .clk(regdec_1_out_5_2[3]));  // open: en, clr
  Register register_4 (.D(controlled_buffer_1_out), .Q(register_4_q), .clk(regdec_1_out_5_2[1]));  // open: en, clr
  assign controlled_buffer_1_out = regdec_1_out_5_2[2] ? register_3_q : 8'bz;  // Controlled_Buffer controlled_buffer_3
  assign controlled_buffer_1_out = regdec_1_out_5_2[0] ? register_4_q : 8'bz;  // Controlled_Buffer controlled_buffer_4
  Register register_5 (.D(controlled_buffer_1_out), .Q(register_5_q), .clk(regdec_1_out_5[7]));  // open: en, clr
  T_Flip_Flop t_ff_1 (.clk(not_1_out), .T(not_1_out), .Q(t_ff_1_q[0]));  // open: Qn, preset, reset, en
  not not_1 (not_1_out, clock_1_out);
  T_Flip_Flop t_ff_2 (.clk(clock_1_out), .T(clock_1_out), .Q(t_ff_1_q[1]));  // open: Qn, preset, reset, en
  Clock clock_1 (.out(clock_1_out));
  Register register_6 (.D(controlled_buffer_1_out), .Q(register_6_q), .clk(regdec_1_out_5[5]));  // open: en, clr
  assign controlled_buffer_1_out = regdec_1_out_5[6] ? register_5_q : 8'bz;  // Controlled_Buffer controlled_buffer_5
  Register #(.width(16)) register_7 (.Q(register_7_q));  // open: D, en, clk, clr
  Counter #(.width(4), .max('hf)) counter_1 (
    .Q(counter_1_q), .clk(decoder_1_out0));  // open: load, D, count, carry, clr
  Decoder #(.select(2), .disabled(0), .enable("false")) decoder_1 (
    .out0(decoder_1_out0), .out1(decoder_1_out1), .out2(decoder_1_out2), .out3(decoder_1_out3), .sel(t_ff_1_q));
  assign controlled_buffer_1_out = regdec_1_out_5[2] ? register_8_q : 8'bz;  // Controlled_Buffer controlled_buffer_6
  assign controlled_buffer_1_out = regdec_1_out_5[4] ? register_6_q : 8'bz;  // Controlled_Buffer controlled_buffer_7
  Register register_8 (.D(controlled_buffer_1_out), .Q(register_8_q), .clk(regdec_1_out_5[3]));  // open: en, clr
  or or_1 (or_1_out, decoder_1_out1, decoder_1_out2, decoder_1_out3);
  Register register_9 (.D(controlled_buffer_1_out), .Q(register_9_q), .clk(regdec_1_out_5[1]));  // open: en, clr
  assign controlled_buffer_1_out = regdec_1_out_5[0] ? register_9_q : 8'bz;  // Controlled_Buffer controlled_buffer_8
  ROM #(.addrWidth(22)) rom_1 (.addr({GT__EQ, register_7_q, counter_1_q}));  // open: data, sel
  // Probe on shreg_1_out_3
  shreg shreg_1 (.in_1(controlled_buffer_1_out), .in_2(in_8), .out_3(shreg_1_out_3));
  // Probe on controlled_buffer_1_out
  regdec regdec_1 (
    .out_5({regdec_1_out_5_2[6], regdec_1_out_5_2[4], regdec_1_out_5_2[2], regdec_1_out_5_2[0], regdec_1_out_5[6], regdec_1_out_5[4], regdec_1_out_5[2], regdec_1_out_5[0]}),
    .in_2(in_11), .in_1(in_9),
    .out_6({regdec_1_out_5_2[7], regdec_1_out_5_2[5], regdec_1_out_5_2[3], regdec_1_out_5_2[1], regdec_1_out_5[7], regdec_1_out_5[5], regdec_1_out_5[3], regdec_1_out_5[1]}),
    .in_3(in_10), .in_4(in_12));
  assign controlled_buffer_9_out = in_4 ? counter_2_q : 16'bz;  // Controlled_Buffer controlled_buffer_9
  Counter #(.width(16), .max('hffff)) counter_2 (
    .load(in_1), .D(shreg_1_out_3), .count(in_3), .Q(counter_2_q), .clk(in_7));  // open: carry, clr
  // Probe on controlled_buffer_1_out
  Register #(.width(16)) register_10 (.D(controlled_buffer_9_out), .Q(register_10_q), .clk(in_2));  // open: en, clr
  RAM #(.addrWidth(16)) ram_1 (
    .addr(register_10_q), .data(controlled_buffer_1_out), .clk(in_5), .ld(in_6));  // open: sel, clr
  Register register_11 (.D(controlled_buffer_1_out), .Q(register_11_q));  // open: en, clk, clr
  ALU alu_1 ();
endmodule

module shreg (
  input  [7:0] in_1,
  input  in_2,
  output [15:0] out_3
);

  Register register_1 (.D(in_1), .Q(out_3[7:0]), .clk(in_2));  // open: en, clr
  Register register_2 (.D(out_3[7:0]), .Q(out_3[15:8]), .clk(in_2));  // open: en, clr
endmodule

module regdec (
  input  in_1,
  input  [2:0] in_2,
  input  in_3,
  input  [2:0] in_4,
  output [7:0] out_5,
  output [7:0] out_6
);

  Decoder #(.select(3), .disabled(0)) decoder_1 (
    .out0(out_5[0]), .out1(out_5[1]), .out2(out_5[2]), .out3(out_5[3]), .out4(out_5[4]), .out5(out_5[5]),
    .out6(out_5[6]), .out7(out_5[7]), .sel(in_2), .en(in_1));
  Decoder #(.select(3), .disabled(0)) decoder_2 (
    .out0(out_6[0]), .out1(out_6[1]), .out2(out_6[2]), .out3(out_6[3]), .out4(out_6[4]), .out5(out_6[5]),
    .out6(out_6[6]), .out7(out_6[7]), .sel(in_4), .en(in_3));
endmodule
